# Fritzing sketch Layout (saved by Fritzing 0.9.4)

parts:
  J1 = Basic Servo
  submit = Momentary Switch [package=ksa_sealed_tac_switch]
  reset = Momentary Switch [package=ksa_sealed_tac_switch]
  LCD1 = LCD screen
  Onderdeel1 = Arduino Nano (Rev3.0)
  LED1 = smd LED [color="Green (555nm)" package="0603 [SMD]"]
  LED2 = smd LED [color="Green (555nm)" package="0603 [SMD]"]
  LED3 = smd LED [color="Green (555nm)" package="0603 [SMD]"]
  LED4 = smd LED [color="Red (633nm)" package="0603 [SMD]"]
  R1 = Resistor [tolerance=±5% resistance=220 package="2512 [SMD]"]
  R2 = Resistor [tolerance=±5% resistance=220 package="2512 [SMD]"]
  R3 = Resistor [tolerance=±5% resistance=220 package="2512 [SMD]"]
  R4 = Resistor [tolerance=±5% resistance=220 package="2512 [SMD]"]
  U1 = POT [package=alps_pot]
  R5 = Resistor [tolerance=±5% resistance=220 package="2512 [SMD]"]
  R6 = Resistor [tolerance=±5% resistance=220 package="2512 [SMD]"]
  J2 = Basic Servo
  R7 = Resistor [tolerance=±5% resistance=220 package="2512 [SMD]"]
  BAT1 = BC9VPC [package=bc9vpc]
  S1 = Momentary Switch [package=ksa_sealed_tac_switch]

nets:
  GND: J1.gnd, LCD1.VSS, LCD1.V0, LCD1.LED-, Onderdeel1.GND, LED1.cathode, LED2.cathode, LED3.cathode, LED4.cathode, U1.E, R5.Pin_1, R6.Pin_1, J2.gnd, BAT1.V-, S1.1
  VCC: J1.vcc, submit.4, reset.4, LCD1.VDD, Onderdeel1.5V, U1.A, J2.vcc, R7.Pin_0
  N1: J1.pulse, Onderdeel1.D6, J2.pulse
  N2: submit.1, Onderdeel1.D13/SCK
  N3: submit.2, R5.Pin_0
  N4: reset.1, Onderdeel1.A1
  N5: reset.2, R6.Pin_0
  N6: LCD1.RS, Onderdeel1.D12/MISO
  N7: LCD1.E, Onderdeel1.D7
  N8: LCD1.DB4, Onderdeel1.D8
  N9: LCD1.DB5, Onderdeel1.D9
  N10: LCD1.DB6, Onderdeel1.D10
  N11: LCD1.DB7, Onderdeel1.D11/MOSI
  N12: Onderdeel1.D2, R1.Pin_1
  N13: Onderdeel1.D3, R2.Pin_1
  N14: Onderdeel1.D4, R3.Pin_1
  N15: Onderdeel1.D5, R4.Pin_1
  N16: Onderdeel1.VIN, BAT1.V+
  N17: Onderdeel1.A2, S1.4
  N18: Onderdeel1.A0, U1.S
