# Fritzing sketch PCB (saved by Fritzing 0.9.4)
circuit board: 4.71994cm x 5.38283cm
breadboards: 1

parts:
  Onderdeel1 = Arduino Nano (Rev3.0)
  R1 = Resistor [tolerance=±5% resistance=220 package=THT]
  R2 = Resistor [tolerance=±5% resistance=220 package=THT]
  R3 = Resistor [tolerance=±5% resistance=220 package=THT]
  R4 = Resistor [tolerance=±5% resistance=220 package=THT]
  R5 = Resistor [tolerance=±5% resistance=220 package=THT]
  R6 = Resistor [tolerance=±5% resistance=220 package=THT]
  R7 = Resistor [tolerance=±5% resistance=220 package=THT]

nets:
  N1: Onderdeel1.D2, R1.Pin_1
  N2: Onderdeel1.D3, R2.Pin_1
  N3: Onderdeel1.D4, R3.Pin_1
  N4: Onderdeel1.D5, R4.Pin_1
  N5: Onderdeel1.GND, R6.Pin_0, R7.Pin_0
  N6: Onderdeel1.5V, R5.Pin_0

notes:
  RLED1
  GLED3
  GLED2
  GLED1
  RBD
  ABD
  Servo
  LCDE
  LCDDB4
  LCDDB5
  LCDDB6
  LCDDB7
  LCDRS
  POTD
  ABG
  LCDP
  GND
  5V
  RBG
  SB
